# Fritzing sketch Gpio.Test.MCP3008 (saved by Fritzing 0.7.10b)
breadboards: 1

parts:
  IC1 = MCP3008 8-channel 10-bit ADC [part_number=MCP3008]  # not connected
  R1 = Resistor [tolerance=±5% resistance=10k package=THT]
  T1 = TMP36 Temperature Sensor [package="TO92 [THT]"]
  R2 = Photocell (LDR) [package=THT]
  RaspberryPi1 = Raspberry Pi Model B

nets:
  GND: R1.Pin_0, T1.GND, RaspberryPi1.GND
  N1: R1.Pin_1, R2.pin_1
  N2: T1.+Vs, R2.pin_0, RaspberryPi1.3V3
  N3: RaspberryPi1.#17, RaspberryPi1.#18
  N4: RaspberryPi1.#22, RaspberryPi1.#23
  N5: RaspberryPi1.MISO, RaspberryPi1.#25

notes:
  Resistor 10kΩ
  Light resistor VT901, 10-27kΩ
  Temperature sensor TMP36

custom parts:
  Raspberry Pi Model B: Raspberry Pi (Model B)
