# Fritzing sketch Gpio.Test.Chaser (saved by Fritzing 0.7.10b)
breadboards: 1

parts:
  R1 = Resistor [tolerance=±5% resistance=10k package=THT]
  R2 = Resistor [tolerance=±5% resistance=10k package=THT]
  R4 = Resistor [tolerance=±5% resistance=10k package=THT]
  R5 = Resistor [tolerance=±5% resistance=10k package=THT]
  R6 = Resistor [tolerance=±5% resistance=10k package=THT]
  R8 = Resistor [tolerance=±5% resistance=10k package=THT]
  LED1 = LED - 5mm [color="Red (633nm)" package="5 mm [THT]"]
  LED2 = LED - 5mm [color="Green (555nm)" package="5 mm [THT]"]
  LED3 = LED - 5mm [color="Yellow (595nm)" package="5 mm [THT]"]
  LED4 = LED - 5mm [color="Red (633nm)" package="5 mm [THT]"]
  LED5 = LED - 5mm [color="Green (555nm)" package="5 mm [THT]"]
  LED6 = LED - 5mm [color="Yellow (595nm)" package="5 mm [THT]"]
  S1 = Pushbutton [package="[THT]"]
  RaspberryPi1 = Raspberry Pi Model B

nets:
  N1: R1.Pin_0, RaspberryPi1.#21
  N2: R1.Pin_1, LED5.anode
  N3: R2.Pin_0, RaspberryPi1.#17
  N4: R2.Pin_1, LED6.anode
  N5: R4.Pin_0, RaspberryPi1.#22
  N6: R4.Pin_1, LED4.anode
  N7: R5.Pin_0, RaspberryPi1.CS0
  N8: R5.Pin_1, LED2.anode
  N9: R6.Pin_0, RaspberryPi1.CS1
  N10: R6.Pin_1, LED1.anode
  N11: R8.Pin_0, RaspberryPi1.#25
  N12: R8.Pin_1, LED3.anode
  N13: LED1.cathode, LED2.cathode, LED3.cathode, LED4.cathode, LED5.cathode, LED6.cathode, S1.Pin_3, S1.Pin_4, RaspberryPi1.GND
  N14: S1.Pin_1, S1.Pin_2, RaspberryPi1.SDA

notes:
  10K resistors

custom parts:
  Raspberry Pi Model B: Raspberry Pi (Model B)
