# Fritzing sketch Test.Gpio.HCSR04 (saved by Fritzing 0.7.11b)
breadboards: 1
perfboards: 1

parts:
  RaspberryPi1 = Raspberry Pi Model B
  HC-SR04 = IC, SIP package, 4 pins [spacing=300mil]  # not connected
  R2 = Resistor [tolerance=±5% resistance=220 package=THT]
  R3 = Resistor [tolerance=±5% resistance=220 package=THT]

nets:
  N1: RaspberryPi1.#4, R2.Pin_0, R3.Pin_0
  N2: R2.Pin_1, R3.Pin_1

custom parts:
  Raspberry Pi Model B: Raspberry Pi (Model B)
