# Fritzing sketch Test.Gpio.MCP23017 (saved by Fritzing 0.7.11b)
breadboards: 1

parts:
  RaspberryPi1 = Raspberry Pi Model B
  IC1 = MCP23017 I2C I/O Expander
  LED1 = LED - 5mm [color="Red (633nm)" package="5 mm [THT]"]
  R1 = 330 Ω Resistor [package=THT]

nets:
  3V3: RaspberryPi1.3V3, IC1.VDD, IC1.RESET
  N1: RaspberryPi1.SDA, IC1.SDA
  N2: RaspberryPi1.SCL, IC1.SCL
  GND: RaspberryPi1.GND, IC1.VSS, IC1.A0, IC1.A1, IC1.A2, R1.Pin_0
  N3: IC1.GPB0, LED1.anode
  N4: LED1.cathode, R1.Pin_1

custom parts:
  Raspberry Pi Model B: Raspberry Pi (Model B)
  MCP23017 I2C I/O Expander: MCP23017 I2C 16-Channel I/O Expander
