# Fritzing sketch Test.Gpio.HD44780 (saved by Fritzing 0.7.10b)
breadboards: 1

parts:
  RaspberryPi1 = Raspberry Pi Model B
  POT1 = Breadboard Trimpot
  LCD1 = LCD screen

nets:
  3V3: RaspberryPi1.3V3, RaspberryPi1.SDA, RaspberryPi1.#17, POT1.PIN1, LCD1.VDD, LCD1.DB7, LCD1.LED+
  GND: RaspberryPi1.GND, RaspberryPi1.TXD, POT1.PIN3, LCD1.VSS, LCD1.R/W, LCD1.LED-
  N1: RaspberryPi1.#21, LCD1.DB6
  N2: RaspberryPi1.#22, LCD1.DB5
  N3: RaspberryPi1.#23, LCD1.DB4
  N4: RaspberryPi1.#24, LCD1.E
  N5: RaspberryPi1.#25, LCD1.RS
  N6: POT1.PIN2, LCD1.V0

custom parts:
  Raspberry Pi Model B: Raspberry Pi (Model B)
